// Logisim project project_new.circ as structural Verilog: 21 circuits, main circuit REG_IR
module main (
  input  [3:0] INPR,
  output [3:0] out_2,
  output E,
  output [3:0] out_4
);

  wire and_1_out, CLK_out, main_control_1_dr, main_control_1_e, main_control_1_hlt, main_control_1_outr_ld;
  wire [1:0] main_control_1_ir, main_control_1_mr;
  wire [2:0] main_control_1_ar, main_control_1_pc;
  wire [3:0] AR_output, DR_output, IR_out_4, IR_out_5, main_control_1_ac, n4_bitlik_alu_1_output_ac,
       PC_output, undriven;
  wire [6:0] main_control_1_alu;
  wire [7:0] controlled_buffer_1_out, ram_1_data;

  Clock CLK (.out(CLK_out));
  MAIN_CONTROL main_control_1 (
    .IR_4_7(IR_out_5), .CLK(and_1_out), .HLT(main_control_1_hlt), .E(main_control_1_e),
    .IR(main_control_1_ir), .MR(main_control_1_mr), .AR(main_control_1_ar), .PC(main_control_1_pc),
    .DR(main_control_1_dr), .AC(main_control_1_ac), .OUTR_LD(main_control_1_outr_ld), .ALU(main_control_1_alu));
  and and_1 (and_1_out, ~main_control_1_hlt, CLK_out);  // AND_Gate
  _4_Bitlik_ALU u_4_bitlik_alu_1 (
    .AC(out_2), .DR(DR_output), .INPR(INPR), .AND(main_control_1_alu[0]), .ADD(main_control_1_alu[1]),
    .CMA(main_control_1_alu[2]), .LD_DR(main_control_1_alu[3]), .LD_INPR(main_control_1_alu[4]),
    .CIR(main_control_1_alu[5]), .CIL(main_control_1_alu[6]), .CLK(and_1_out),
    .Output_AC(n4_bitlik_alu_1_output_ac), .E(E), .CLR(main_control_1_e));  // open: Cin
  \_4_BİT_KAYDE4_BİT_KAYDEDİCİ_DEVRESİ  AR (
    .INPUT(controlled_buffer_1_out[3:0]), .CLK(and_1_out), .LD(main_control_1_ar[0]),
    .INC(main_control_1_ar[2]), .OUTPUT(AR_output));  // open: CLR
  \_4_BİT_KAYDE4_BİT_KAYDEDİCİ_DEVRESİ  PC (
    .INPUT(controlled_buffer_1_out[3:0]), .CLK(and_1_out), .LD(main_control_1_pc[0]),
    .INC(main_control_1_pc[1]), .OUTPUT(PC_output));  // open: CLR
  \_4_BİT_KAYDE4_BİT_KAYDEDİCİ_DEVRESİ  DR (
    .INPUT(controlled_buffer_1_out[3:0]), .CLK(and_1_out), .LD(main_control_1_dr), .OUTPUT(DR_output));  // open: INC, CLR
  \_4_BİT_KAYDE4_BİT_KAYDEDİCİ_DEVRESİ  AC (
    .INPUT(n4_bitlik_alu_1_output_ac), .CLK(and_1_out), .LD(main_control_1_ac[0]),
    .INC(main_control_1_ac[2]), .CLR(main_control_1_ac[1]), .OUTPUT(out_2));
  // Probe on IR_out_5
  REG_IR IR (
    .INPUT(controlled_buffer_1_out), .CLK(and_1_out), .LD(main_control_1_ir[0]), .out_4(IR_out_4),
    .out_5(IR_out_5));
  \_4_BİT_KAYDE4_BİT_KAYDEDİCİ_DEVRESİ  OUTR (
    .INPUT(controlled_buffer_1_out[3:0]), .CLK(and_1_out), .LD(main_control_1_outr_ld), .OUTPUT(out_4));  // open: INC, CLR
  RAM #(.addrWidth(4), .bus("separate")) ram_1 (
    .addr(AR_output), .din(controlled_buffer_1_out), .data(ram_1_data), .str(main_control_1_mr[1]),
    .clk(and_1_out));  // open: sel, ld, clr
  // Probe on AR_output
  // Probe on PC_output
  // Probe on DR_output
  // Probe on out_2
  // Probe on IR_out_4
  assign controlled_buffer_1_out = main_control_1_mr[0] ? ram_1_data : 8'bz;  // Controlled_Buffer controlled_buffer_1
  assign controlled_buffer_1_out = main_control_1_ar[1] ? {4'b0000, AR_output} : 8'bz;  // Controlled_Buffer controlled_buffer_2
  assign controlled_buffer_1_out = main_control_1_pc[2] ? {4'b0000, PC_output} : 8'bz;  // Controlled_Buffer controlled_buffer_3
  assign controlled_buffer_1_out = main_control_1_ac[3] ? {4'b0000, out_2} : 8'bz;  // Controlled_Buffer controlled_buffer_4
  assign controlled_buffer_1_out = main_control_1_ir[1] ? {undriven, IR_out_4} : 8'bz;  // Controlled_Buffer controlled_buffer_5
endmodule

module _2_Bit_Counter (
  input  CLK,
  input  CLR,
  output Q1,
  output Q0
);

  J_K_Flip_Flop j_k_ff_1 (.J(Q0), .clk(CLK), .K(Q0), .Q(Q1), .reset(CLR));  // open: Qn, preset, en
  J_K_Flip_Flop j_k_ff_2 (.J(1'b1), .clk(CLK), .K(1'b1), .Q(Q0), .reset(CLR));  // open: Qn, preset, en
endmodule

// Counter
module _4_Bit_Counter (
  input  CLK,
  input  CLR,
  output [3:0] OUT
);

  wire d_ff_1_q, nand_1_out;

  D_Flip_Flop d_ff_1 (.clk(CLK), .D(CLR), .Q(d_ff_1_q));  // open: Qn, preset, en, reset
  _2_Bit_Counter u_2_bit_counter_1 (.CLK(nand_1_out), .CLR(d_ff_1_q), .Q1(OUT[3]), .Q0(OUT[2]));
  _2_Bit_Counter u_2_bit_counter_2 (.CLK(CLK), .CLR(d_ff_1_q), .Q1(OUT[1]), .Q0(OUT[0]));
  nand nand_1 (nand_1_out, OUT[0], OUT[1]);
endmodule

// ALU
module _4_Bitlik_ALU (
  input  Cin,
  input  [3:0] AC,
  input  [3:0] DR,
  input  [3:0] INPR,
  input  AND,
  input  ADD,
  input  CMA,
  input  LD_DR,
  input  LD_INPR,
  input  CIR,
  input  CIL,
  input  CLK,
  input  CLR,
  output [3:0] Output_AC,
  output E
);

  wire e_con_1_ac_0_2, e_con_1_ac_3_2, n1_bitlik_alu_1_cout, n1_bitlik_alu_2_cout, n1_bitlik_alu_3_cout,
       n1_bitlik_alu_4_cout;

  _1_Bitlik_ALU u_1_bitlik_alu_1 (
    .AND(AND), .ADD(ADD), .CMA(CMA), .LD_DR(LD_DR), .LD_INPR(LD_INPR), .CIR(CIR), .CIL(CIL),
    .AC_i_1(e_con_1_ac_0_2), .AC_i_1_2(AC[1]), .INPR(INPR[0]), .DR(DR[0]), .AC(AC[0]), .Cin(Cin),
    .Cout(n1_bitlik_alu_1_cout), .Output_AC(Output_AC[0]));
  _1_Bitlik_ALU u_1_bitlik_alu_2 (
    .AND(AND), .ADD(ADD), .CMA(CMA), .LD_DR(LD_DR), .LD_INPR(LD_INPR), .CIR(CIR), .CIL(CIL), .AC_i_1(AC[0]),
    .AC_i_1_2(AC[2]), .INPR(INPR[1]), .DR(DR[1]), .AC(AC[1]), .Cin(n1_bitlik_alu_1_cout),
    .Cout(n1_bitlik_alu_2_cout), .Output_AC(Output_AC[1]));
  _1_Bitlik_ALU u_1_bitlik_alu_3 (
    .AND(AND), .ADD(ADD), .CMA(CMA), .LD_DR(LD_DR), .LD_INPR(LD_INPR), .CIR(CIR), .CIL(CIL), .AC_i_1(AC[1]),
    .AC_i_1_2(AC[3]), .INPR(INPR[2]), .DR(DR[2]), .AC(AC[2]), .Cin(n1_bitlik_alu_2_cout),
    .Cout(n1_bitlik_alu_3_cout), .Output_AC(Output_AC[2]));
  _1_Bitlik_ALU u_1_bitlik_alu_4 (
    .AND(AND), .ADD(ADD), .CMA(CMA), .LD_DR(LD_DR), .LD_INPR(LD_INPR), .CIR(CIR), .CIL(CIL), .AC_i_1(AC[2]),
    .AC_i_1_2(e_con_1_ac_3_2), .INPR(INPR[3]), .DR(DR[3]), .AC(AC[3]), .Cin(n1_bitlik_alu_3_cout),
    .Cout(n1_bitlik_alu_4_cout), .Output_AC(Output_AC[3]));
  E_CON e_con_1 (
    .AC_3(AC[3]), .CIL(CIL), .AC_0(AC[0]), .CIR(CIR), .COUT(n1_bitlik_alu_4_cout), .ADD(ADD), .CLK(CLK),
    .CLR(CLR), .AC_0_2(e_con_1_ac_0_2), .E(E), .AC_3_2(e_con_1_ac_3_2));
endmodule

// AC
module _1_Bitlik_ALU (
  input  INPR,
  input  DR,
  input  AC,
  input  AND,
  input  ADD,
  input  Cin,
  input  CMA,
  input  LD_DR,
  input  LD_INPR,
  input  CIR,
  input  CIL,
  input  AC_i_1,
  input  AC_i_1_2,
  output Cout,
  output Output_AC
);

  wire Add_out, adder_1_out, And_out, Comp_out, Id_DR_out, Id_INPR_out, not_1_out, Shl_out, Shr_out;

  Adder #(.width(1)) adder_1 (.a(AC), .b(DR), .out(adder_1_out), .cin(Cin), .cout(Cout));
  not not_1 (not_1_out, AC);
  and u_And (And_out, AND, AC, DR);
  and u_Add (Add_out, ADD, adder_1_out);
  and Comp (Comp_out, CMA, not_1_out);
  and Id_DR (Id_DR_out, LD_DR, DR);
  and Id_INPR (Id_INPR_out, LD_INPR, INPR);
  and Shr (Shr_out, CIR, AC_i_1_2);
  and Shl (Shl_out, CIL, AC_i_1);
  or or_1 (Output_AC, And_out, Add_out, Comp_out, Id_DR_out, Id_INPR_out, Shr_out, Shl_out);
endmodule

// 4_REG
module \_4_BİT_KAYDE4_BİT_KAYDEDİCİ_DEVRESİ  (
  input  INC,
  input  LD,
  input  [3:0] INPUT,
  input  CLK,
  input  CLR,
  output [3:0] OUTPUT
);

  wire and_1_out, and_2_out, and_3_out, and_4_out, and_5_out, and_6_out, and_7_out, and_8_out, and_9_out,
       and_10_out, and_11_out, and_12_out, not_1_out, not_2_out, not_3_out, not_4_out, not_5_out, not_6_out,
       or_1_out, or_2_out, or_3_out, or_4_out, or_5_out, or_6_out, or_7_out, or_8_out;

  not not_1 (not_1_out, LD);
  not not_2 (not_2_out, not_1_out);
  not not_3 (not_3_out, INPUT[0]);
  not not_4 (not_4_out, INPUT[1]);
  not not_5 (not_5_out, INPUT[2]);
  not not_6 (not_6_out, INPUT[3]);
  and and_1 (and_1_out, INC, not_1_out);
  and and_2 (and_2_out, not_2_out, INPUT[0]);
  and and_3 (and_3_out, not_2_out, not_3_out);
  and and_4 (and_4_out, not_2_out, INPUT[1]);
  and and_5 (and_5_out, not_2_out, not_4_out);
  and and_6 (and_6_out, not_2_out, INPUT[2]);
  and and_7 (and_7_out, not_2_out, not_5_out);
  and and_8 (and_8_out, not_2_out, INPUT[3]);
  and and_9 (and_9_out, not_2_out, not_6_out);
  and and_10 (and_10_out, and_1_out, OUTPUT[0]);
  and and_11 (and_11_out, and_1_out, OUTPUT[0], OUTPUT[1]);
  and and_12 (and_12_out, OUTPUT[2], OUTPUT[1], OUTPUT[0], and_1_out);
  or or_1 (or_1_out, and_2_out, and_1_out);
  or or_2 (or_2_out, and_3_out, and_1_out);
  or or_3 (or_3_out, and_4_out, and_10_out);
  or or_4 (or_4_out, and_10_out, and_5_out);
  or or_5 (or_5_out, and_6_out, and_11_out);
  or or_6 (or_6_out, and_11_out, and_7_out);
  or or_7 (or_7_out, and_8_out, and_12_out);
  or or_8 (or_8_out, and_12_out, and_9_out);
  J_K_Flip_Flop j_k_ff_1 (.J(or_1_out), .clk(CLK), .K(or_2_out), .Q(OUTPUT[0]), .reset(CLR));  // open: Qn, preset, en
  J_K_Flip_Flop j_k_ff_2 (.J(or_3_out), .clk(CLK), .K(or_4_out), .Q(OUTPUT[1]), .reset(CLR));  // open: Qn, preset, en
  J_K_Flip_Flop j_k_ff_3 (.J(or_5_out), .clk(CLK), .K(or_6_out), .Q(OUTPUT[2]), .reset(CLR));  // open: Qn, preset, en
  J_K_Flip_Flop j_k_ff_4 (.J(or_7_out), .clk(CLK), .K(or_8_out), .Q(OUTPUT[3]), .reset(CLR));  // open: Qn, preset, en
endmodule

module REG_IR (
  input  [7:0] INPUT,
  input  CLK,
  input  LD,
  output [3:0] out_4,
  output [3:0] out_5
);

  \_4_BİT_KAYDE4_BİT_KAYDEDİCİ_DEVRESİ  _0_3 (
    .INPUT(INPUT[3:0]), .CLK(CLK), .LD(LD), .OUTPUT(out_4));  // open: INC, CLR
  \_4_BİT_KAYDE4_BİT_KAYDEDİCİ_DEVRESİ  _4_7 (
    .INPUT(INPUT[7:4]), .CLK(CLK), .LD(LD), .OUTPUT(out_5));  // open: INC, CLR
endmodule

// M[]
module MR (
  input  T1,
  input  T3,
  input  D0,
  input  D1,
  input  D2,
  input  D3,
  input  D5,
  input  D6,
  output MR_BUS,
  output MR_LD
);

  wire and_1_out, and_2_out, and_3_out, and_4_out, and_5_out, and_6_out;

  and and_1 (and_1_out, D0, T3);
  and and_2 (and_2_out, D1, T3);
  and and_3 (and_3_out, D2, T3);
  and and_4 (and_4_out, D6, T3);
  and and_5 (and_5_out, D3, T3);
  and and_6 (and_6_out, D5, T3);
  or or_1 (MR_BUS, T1, and_1_out, and_2_out, and_3_out, and_4_out);
  or or_2 (MR_LD, and_5_out, and_6_out);
endmodule

module AR (
  input  T0,
  input  T2,
  input  T3,
  input  T4,
  input  D4,
  input  D5,
  output AR_LD,
  output AR_BUS,
  output AR_INC
);

  wire and_1_out, and_2_out;

  and and_1 (and_1_out, D4, T3);
  and and_2 (and_2_out, D5, T4);
  or or_1 (AR_LD, T0, T2);
  or or_2 (AR_BUS, and_1_out, and_2_out);
  and and_3 (AR_INC, D5, T3);
endmodule

// PC_control
module PC (
  input  T0,
  input  T1,
  input  T3,
  input  T4,
  input  D4,
  input  D5,
  input  D6,
  output PC_LD,
  output PC_INC,
  output PC_BUS
);

  wire and_1_out, and_2_out, and_3_out, or_1_out;

  or or_1 (or_1_out, D6, D4);
  and and_1 (and_1_out, or_1_out, T3);
  and and_2 (and_2_out, D5, T4);
  and and_3 (and_3_out, D5, T3);
  or or_2 (PC_BUS, and_3_out, T0);
  or or_3 (PC_LD, and_1_out, and_2_out);

  assign PC_INC = T1;
endmodule

module DR (
  input  T3,
  input  T4,
  input  D0,
  input  D1,
  input  D2,
  output DR_LD
);

  wire and_1_out, and_2_out, and_3_out, and_4_out, and_5_out;

  and and_1 (and_1_out, D0, T3);
  and and_2 (and_2_out, D1, T3);
  and and_3 (and_3_out, D2, T3);
  and and_4 (and_4_out, D0, T4);
  and and_5 (and_5_out, D1, T4);
  or or_1 (DR_LD, and_1_out, and_2_out, and_3_out, and_4_out, and_5_out);
endmodule

module IR (
  input  T1,
  input  T2,
  output IR_LD,
  output IR_BUS
);


  assign IR_BUS = T2;
  assign IR_LD = T1;
endmodule

module AC (
  input  T3,
  input  T4,
  input  D0,
  input  D1,
  input  D2,
  input  D3,
  input  D7,
  input  D9,
  input  D10,
  input  D11,
  input  D12,
  input  D13,
  input  D14,
  output AC_LD,
  output AC_CLR,
  output AC_INC,
  output AC_BUS
);

  wire and_1_out, and_2_out, and_3_out, and_4_out, and_5_out, and_6_out, and_7_out, and_8_out, and_9_out;

  and and_1 (and_1_out, D0, T4);
  and and_2 (and_2_out, D1, T4);
  and and_3 (and_3_out, D2, T4);
  and and_4 (and_4_out, D9, T3);
  and and_5 (and_5_out, D11, T3);
  and and_6 (and_6_out, D12, T3);
  and and_7 (and_7_out, D13, T3);
  and CLR (AC_CLR, D7, T3);
  and INC (AC_INC, D10, T3);
  and and_8 (and_8_out, D3, T3);
  and and_9 (and_9_out, D14, T3);
  or or_1 (AC_BUS, and_8_out, and_9_out);
  or or_2 (AC_LD, and_1_out, and_2_out, and_3_out, and_4_out, and_5_out, and_6_out, and_7_out);
endmodule

// SC_CLR
module SC (
  input  T3,
  input  T4,
  input  D0,
  input  D1,
  input  D2,
  input  D3,
  input  D4,
  input  D5,
  input  D6,
  input  D7,
  input  D8,
  input  D9,
  input  D10,
  input  D11,
  input  D12,
  input  D13,
  input  D14,
  output SC_CLR
);

  wire and_1_out, and_2_out, or_1_out, or_2_out;

  or or_1 (or_1_out, D14, D13, D12, D11, D10, D9, D8, D7, D6, D4, D3);
  or or_2 (or_2_out, D5, D2, D1, D0);
  and and_1 (and_1_out, or_1_out, T3);
  and and_2 (and_2_out, or_2_out, T4);
  or or_3 (SC_CLR, and_1_out, and_2_out);
endmodule

module S (
  input  T3,
  input  D15,
  output S_CLR
);

  and and_1 (S_CLR, D15, T3);
endmodule

module E (
  input  T3,
  input  T4,
  input  D1,
  input  D8,
  output E_LD,
  output E_CLR
);

  and and_1 (E_LD, D1, T4);
  and and_2 (E_CLR, D8, T3);
endmodule

module OUTR (
  input  T3,
  input  D14,
  output OUTR_LD
);

  and and_1 (OUTR_LD, D14, T3);
endmodule

// E
module E_CON (
  input  AC_3,
  input  CIL,
  input  AC_0,
  input  CIR,
  input  COUT,
  input  ADD,
  input  CLK,
  input  CLR,
  output AC_0_2,
  output E,
  output AC_3_2
);

  wire and_1_out, and_2_out, and_3_out, d_ff_3_q;

  and and_1 (and_1_out, AC_3, CIL);
  and and_2 (and_2_out, AC_0, CIR);
  and and_3 (and_3_out, COUT, ADD);
  D_Flip_Flop d_ff_1 (.clk(CLK), .D(and_1_out), .Q(AC_0_2), .reset(CLR));  // open: Qn, preset, en
  D_Flip_Flop d_ff_2 (.clk(CLK), .D(and_2_out), .Q(AC_3_2), .reset(CLR));  // open: Qn, preset, en
  D_Flip_Flop d_ff_3 (.clk(CLK), .D(and_3_out), .Q(d_ff_3_q), .reset(CLR));  // open: Qn, preset, en
  or or_1 (E, AC_0_2, AC_3_2, d_ff_3_q);
endmodule

module ALU_CONTROLLER (
  input  T3,
  input  T4,
  input  D0,
  input  D1,
  input  D2,
  input  D9,
  input  D11,
  input  D12,
  input  D13,
  output AND,
  output ADD,
  output CMP,
  output DR_LD,
  output INPR,
  output SHR,
  output SHL
);

  and and_1 (SHR, D11, T3);
  and and_2 (SHL, D12, T3);
  and and_3 (AND, D0, T4);
  and and_4 (ADD, D1, T4);
  and and_5 (CMP, D9, T3);
  and and_6 (DR_LD, D2, T4);
  and and_7 (INPR, D13, T3);
endmodule

module reg_Controller (
  input  T0,
  input  T1,
  input  T2,
  input  T3,
  input  T4,
  input  D0,
  input  D1,
  input  D2,
  input  D3,
  input  D4,
  input  D5,
  input  D6,
  input  D7,
  input  D8,
  input  D9,
  input  D10,
  input  D11,
  input  D12,
  input  D13,
  input  D14,
  output [1:0] MR,
  output [2:0] AR,
  output [2:0] PC,
  output DR,
  output [3:0] AC,
  output OUTR,
  output [1:0] IR
);

  OUTR outr_1 (.T3(T3), .D14(D14), .OUTR_LD(OUTR));
  IR ir_1 (.T1(T1), .T2(T2), .IR_LD(IR[0]), .IR_BUS(IR[1]));
  MR mr_1 (.T1(T1), .T3(T3), .D0(D0), .D1(D1), .D2(D2), .D3(D3), .D5(D5), .D6(D6), .MR_BUS(MR[0]), .MR_LD(MR[1]));
  AR ar_1 (.T0(T0), .T2(T2), .T3(T3), .T4(T4), .D4(D4), .D5(D5), .AR_LD(AR[0]), .AR_BUS(AR[1]), .AR_INC(AR[2]));
  PC pc_1 (
    .T0(T0), .T1(T1), .T3(T3), .T4(T4), .D4(D4), .D5(D5), .D6(D6), .PC_LD(PC[0]), .PC_INC(PC[1]),
    .PC_BUS(PC[2]));
  DR dr_1 (.T3(T3), .T4(T4), .D0(D0), .D1(D1), .D2(D2), .DR_LD(DR));
  AC ac_1 (
    .T3(T3), .T4(T4), .D0(D0), .D1(D1), .D2(D2), .D3(D3), .D7(D7), .D9(D9), .D10(D10), .D11(D11), .D12(D12),
    .D13(D13), .D14(D14), .AC_LD(AC[0]), .AC_CLR(AC[1]), .AC_INC(AC[2]), .AC_BUS(AC[3]));
endmodule

module MAIN_CONTROL (
  input  [3:0] IR_4_7,
  input  CLK,
  output [1:0] MR,
  output [2:0] AR,
  output [2:0] PC,
  output DR,
  output [3:0] AC,
  output [1:0] IR,
  output OUTR_LD,
  output [6:0] ALU,
  output HLT,
  output E
);

  wire decoder_1_out15, sc_1_sc_clr;
  wire [3:0] n4_bit_counter_1_out;
  wire [4:0] decoder_2_out0;
  wire [14:0] decoder_1_out0;

  SC sc_1 (
    .T3(decoder_2_out0[3]), .T4(decoder_2_out0[4]), .D0(decoder_1_out0[0]), .D1(decoder_1_out0[1]),
    .D2(decoder_1_out0[2]), .D3(decoder_1_out0[3]), .D4(decoder_1_out0[4]), .D5(decoder_1_out0[5]),
    .D6(decoder_1_out0[6]), .D7(decoder_1_out0[7]), .D8(decoder_1_out0[8]), .D9(decoder_1_out0[9]),
    .D10(decoder_1_out0[10]), .D11(decoder_1_out0[11]), .D12(decoder_1_out0[12]), .D13(decoder_1_out0[13]),
    .D14(decoder_1_out0[14]), .SC_CLR(sc_1_sc_clr));
  _4_Bit_Counter u_4_bit_counter_1 (.CLK(CLK), .CLR(sc_1_sc_clr), .OUT(n4_bit_counter_1_out));
  Decoder #(.select(4)) decoder_1 (
    .out0(decoder_1_out0[0]), .out1(decoder_1_out0[1]), .out2(decoder_1_out0[2]), .out3(decoder_1_out0[3]),
    .out4(decoder_1_out0[4]), .out5(decoder_1_out0[5]), .out6(decoder_1_out0[6]), .out7(decoder_1_out0[7]),
    .out8(decoder_1_out0[8]), .out9(decoder_1_out0[9]), .out10(decoder_1_out0[10]),
    .out11(decoder_1_out0[11]), .out12(decoder_1_out0[12]), .out13(decoder_1_out0[13]),
    .out14(decoder_1_out0[14]), .out15(decoder_1_out15), .sel(IR_4_7));  // open: en
  Decoder #(.select(4)) decoder_2 (
    .out0(decoder_2_out0[0]), .out1(decoder_2_out0[1]), .out2(decoder_2_out0[2]), .out3(decoder_2_out0[3]),
    .out4(decoder_2_out0[4]), .sel(n4_bit_counter_1_out));  // open: out5, out6, out7, out8, out9, out10, out11, out12, out13, out14, out15, en
  and and_1 (HLT, decoder_1_out15, decoder_2_out0[3]);
  and and_2 (E, decoder_1_out0[8], decoder_2_out0[3]);
  ALU_CONTROLLER alu_controller_1 (
    .T3(decoder_2_out0[3]), .T4(decoder_2_out0[4]), .D0(decoder_1_out0[0]), .D1(decoder_1_out0[1]),
    .D2(decoder_1_out0[2]), .D9(decoder_1_out0[9]), .D11(decoder_1_out0[11]), .D12(decoder_1_out0[12]),
    .D13(decoder_1_out0[13]), .AND(ALU[0]), .ADD(ALU[1]), .CMP(ALU[2]), .DR_LD(ALU[3]), .INPR(ALU[4]),
    .SHR(ALU[5]), .SHL(ALU[6]));
  reg_Controller reg_controller_1 (
    .T0(decoder_2_out0[0]), .T1(decoder_2_out0[1]), .T2(decoder_2_out0[2]), .T3(decoder_2_out0[3]),
    .T4(decoder_2_out0[4]), .D0(decoder_1_out0[0]), .D1(decoder_1_out0[1]), .D2(decoder_1_out0[2]),
    .D3(decoder_1_out0[3]), .D4(decoder_1_out0[4]), .D5(decoder_1_out0[5]), .D6(decoder_1_out0[6]),
    .D7(decoder_1_out0[7]), .D8(decoder_1_out0[8]), .D9(decoder_1_out0[9]), .D10(decoder_1_out0[10]),
    .D11(decoder_1_out0[11]), .D12(decoder_1_out0[12]), .D13(decoder_1_out0[13]), .D14(decoder_1_out0[14]),
    .MR(MR), .AR(AR), .PC(PC), .DR(DR), .AC(AC), .OUTR(OUTR_LD), .IR(IR));

  // Notes on the sheet:
  //   D
  //   T
endmodule
